// Logisim project ALU.circ as structural Verilog: 4 circuits, main circuit main
module main (
  input  [31:0] in_1,
  input  [31:0] in_2,
  input  [4:0] in_3,
  output out_4,
  output out_5,
  output [31:0] out_6,
  output [31:0] out_7
);

  ALU alu_1 (.in_1(in_1), .in_3(in_2), .in_4(in_3), .out_5(out_6), .out_7(out_5), .out_8(out_4));  // open: in_2, out_6
endmodule

module ALU (
  input  [31:0] in_1,
  input  [15:0] in_2,
  input  [31:0] in_3,
  input  [4:0] in_4,
  output [31:0] out_5,
  output [31:0] out_6,
  output out_7,
  output out_8
);

  wire CARRY_S, comparator_1_eq, comparator_2_eq;
  wire [31:0] AND, D_C, DIV, DIV_U, M_C, MUL, MUL_U, NOR, OR, SUB, SUM, undriven, undriven_2, undriven_3,
       undriven_4, undriven_5, undriven_6, XOR;

  Multiplexer #(.width(32)) multiplexer_1 (.in0(D_C), .in1(M_C), .out(out_6), .sel(CARRY_S));  // open: en
  Comparator #(.width(5)) comparator_1 (.a(in_4), .b(5'b00010), .eq(comparator_1_eq));  // open: gt, lt
  Comparator #(.width(5)) comparator_2 (.a(5'b00100), .b(in_4), .eq(comparator_2_eq));  // open: gt, lt
  or or_1 (CARRY_S, comparator_1_eq, comparator_2_eq);
  Adder #(.width(32)) adder_1 (.a(in_1), .b(in_3), .out(SUM));  // open: cin, cout
  Divider_U_S divider_u_s_1 (.in_1(1'b0), .in_2(in_1), .in_3(in_3), .out_4(DIV), .out_5(D_C));
  Multiplexer #(.select(5), .width(32)) multiplexer_2 (
    .in0(SUM), .in1(SUB), .in2(MUL), .in3(DIV), .in4(MUL_U), .in5(DIV_U), .in8(AND), .in9(OR), .in10(NOR),
    .in11(XOR), .in12(undriven), .in13(undriven_4), .in14(undriven_2), .in15(undriven_5), .in16(undriven_3),
    .in17(undriven_6), .out(out_5), .sel(in_4));  // open: in6, in7, in18, in19, in20, in21, in22, in23, in24, in25, in26, in27, in28, in29, in30, in31, en
  Comparator #(.width(32)) comparator_3 (.a(out_5), .b({32{1'b0}}), .eq(out_7), .lt(out_8));  // open: gt
  Subtractor #(.width(32)) subtractor_1 (.a(in_1), .b(in_3), .out(SUB));  // open: bin, bout
  Multiplier_U_S multiplier_u_s_1 (.in_1(1'b0), .in_2(in_1), .in_3(in_3), .out_4(MUL), .out_5(M_C));
  assign AND = in_1 & in_3;  // AND_Gate and_1, 32 bits wide
  Multiplier_U_S multiplier_u_s_2 (.in_1(1'b1), .in_2(in_1), .in_3(in_3), .out_4(MUL_U), .out_5(M_C));
  assign OR = in_1 | in_3;  // OR_Gate or_2, 32 bits wide
  Divider_U_S divider_u_s_2 (.in_1(1'b1), .in_2(in_1), .in_3(in_3), .out_4(DIV_U), .out_5(D_C));
  assign XOR = in_1 ^ in_3;  // XOR_Gate xor_1, 32 bits wide
  assign NOR = ~(in_1 | in_3);  // NOR_Gate nor_1, 32 bits wide

  // Other names for the same wires on the sheet: A[31:0] = in_1; B[31:0] = in_3; C[15:0] = in_2; Carry[31:0] = out_6;
  //   CERO_flag = out_7; N_flag = out_8; OP[4:0] = in_4; S[31:0] = out_5

  // Notes on the sheet:
  //   ALU
  //   INPUT
  //   OUTPUT
  //   OPERACIONES
  //   SUMA
  //   DIVISIÓN
  //   SUMA
  //   RESTA
  //   MULTIPLICACIÓN
  //   SUMA
  //   AND LOGIC
  //   MULTIPLICACIÓN U
  //   SUMA
  //   SUMA
  //   OR LOGIC
  //   DIVISIÓN U
  //   XOR
  //   NOR
endmodule

module Multiplier_U_S (
  input  in_1,
  input  [31:0] in_2,
  input  [31:0] in_3,
  output [31:0] out_4,
  output [31:0] out_5
);

  wire SEL_A, SEL_B, SEL_M;
  wire [31:0] A_prime, B_prime, M_prime, negator_1_out, negator_2_out, negator_3_out;

  Multiplexer #(.width(32)) multiplexer_1 (.in0(in_2), .in1(negator_1_out), .out(A_prime), .sel(SEL_A));  // open: en
  Negator #(.width(32)) negator_1 (.in(in_2), .out(negator_1_out));
  Multiplexer #(.width(32)) multiplexer_2 (.in0(in_3), .in1(negator_2_out), .out(B_prime), .sel(SEL_B));  // open: en
  Negator #(.width(32)) negator_2 (.in(in_3), .out(negator_2_out));
  Multiplexer #(.width(32)) multiplexer_3 (.in0(M_prime), .in1(negator_3_out), .out(out_4), .sel(SEL_M));  // open: en
  Negator #(.width(32)) negator_3 (.in(M_prime), .out(negator_3_out));
  Multiplier #(.width(32)) multiplier_1 (.a(A_prime), .b(B_prime), .out(M_prime), .cout(out_5));  // open: cin
  and and_1 (SEL_A, in_2[31], in_1);
  and and_2 (SEL_B, in_1, in_3[31]);
  and and_3 (SEL_M, in_1, M_prime[31]);

  // Other names for the same wires on the sheet: A[31:0] = in_2; A_S = in_2[31]; B[31:0] = in_3; B_S = in_3[31];
  //   M[31:0] = out_4; M_C[31:0] = out_5; M_prime_S = M_prime[31]; Selector_S_U = in_1

  // Notes on the sheet:
  //   MULTIPLIER
  //   U
  //   NSIGNED
  //   IGNED
  //   S
  //   \
endmodule

module Divider_U_S (
  input  in_1,
  input  [31:0] in_2,
  input  [31:0] in_3,
  output [31:0] out_4,
  output [31:0] out_5
);

  wire SEL_A, SEL_B, SEL_D;
  wire [31:0] A_prime, B_prime, D_prime, negator_1_out, negator_2_out, negator_3_out;

  Multiplexer #(.width(32)) multiplexer_1 (.in0(in_2), .in1(negator_1_out), .out(A_prime), .sel(SEL_A));  // open: en
  Negator #(.width(32)) negator_1 (.in(in_2), .out(negator_1_out));
  Multiplexer #(.width(32)) multiplexer_2 (.in0(in_3), .in1(negator_2_out), .out(B_prime), .sel(SEL_B));  // open: en
  Negator #(.width(32)) negator_2 (.in(in_3), .out(negator_2_out));
  Multiplexer #(.width(32)) multiplexer_3 (.in0(D_prime), .in1(negator_3_out), .out(out_4), .sel(SEL_D));  // open: en
  Negator #(.width(32)) negator_3 (.in(D_prime), .out(negator_3_out));
  Divider #(.width(32)) divider_1 (.a(A_prime), .b(B_prime), .out(D_prime), .rem(out_5));  // open: upper
  and and_1 (SEL_A, in_2[31], in_1);
  and and_2 (SEL_B, in_1, in_3[31]);
  and and_3 (SEL_D, in_1, D_prime[31]);

  // Other names for the same wires on the sheet: A[31:0] = in_2; A_S = in_2[31]; B[31:0] = in_3; B_S = in_3[31];
  //   D[31:0] = out_4; D_C[31:0] = out_5; D_prime_S = D_prime[31]; Selector_S_U = in_1

  // Notes on the sheet:
  //   DIVIDER
  //   U
  //   NSIGNED
  //   IGNED
  //   S
  //   \
endmodule
