// Logisim project Register File.circ as structural Verilog: 2 circuits, main circuit main
module main (
  input  [31:0] in_1,
  input  [4:0] in_2,
  input  in_3,
  input  in_4,
  input  [4:0] in_5,
  input  [4:0] in_6,
  output [31:0] out_7,
  output [31:0] out_8
);

  wire clock_1_out;

  // Probe on in_1
  Clock clock_1 (.out(clock_1_out));
  RegisterFile registerfile_1 (
    .in_1(in_5), .in_2(in_1), .in_3(in_6), .in_7(in_3), .in_4(clock_1_out), .in_6(in_2), .in_5(in_4),
    .out_8(out_7), .out_9(out_8));
endmodule

module RegisterFile (
  input  [4:0] in_1,
  input  [31:0] in_2,
  input  [4:0] in_3,
  input  in_4,
  input  in_5,
  input  [4:0] in_6,
  input  in_7,
  output [31:0] out_8,
  output [31:0] out_9
);

  wire e0, e1, e2, e3, e4, e5, e6, e7, e8, e9, e10, e11, e12, e13, e14, e15, e16, e17, e18, e19, e20, e21,
       e22, e23, e24, e25, e26, e27, e28, e29, e30, e31;
  wire [31:0] s1, s2, s3, s4, s5, s6, s7, s8, s9, s10, s11, s12, s13, s14, s15, s16, s17, s18, s19, s20, s21,
       s22, s23, s24, s25, s26, s27, s28, s29, s30, s31;

  Register #(.width(32)) R1 (.D(in_2), .en(e1), .Q(s1), .clk(in_4), .clr(in_5));
  Register #(.width(32)) R7 (.D(in_2), .en(e7), .Q(s7), .clk(in_4), .clr(in_5));
  Register #(.width(32)) R13 (.D(in_2), .en(e13), .Q(s13), .clk(in_4), .clr(in_5));
  Register #(.width(32)) R19 (.D(in_2), .en(e19), .Q(s19), .clk(in_4), .clr(in_5));
  Register #(.width(32)) R25 (.D(in_2), .en(e25), .Q(s25), .clk(in_4), .clr(in_5));
  Register #(.width(32)) R31 (.D(in_2), .en(e31), .Q(s31), .clk(in_4), .clr(in_5));
  Register #(.width(32)) R2 (.D(in_2), .en(e2), .Q(s2), .clk(in_4), .clr(in_5));
  Register #(.width(32)) R8 (.D(in_2), .en(e8), .Q(s8), .clk(in_4), .clr(in_5));
  Register #(.width(32)) R14 (.D(in_2), .en(e14), .Q(s14), .clk(in_4), .clr(in_5));
  Register #(.width(32)) R20 (.D(in_2), .en(e20), .Q(s20), .clk(in_4), .clr(in_5));
  Register #(.width(32)) R26 (.D(in_2), .en(e26), .Q(s26), .clk(in_4), .clr(in_5));
  Decoder #(.select(5)) decoder_1 (
    .out0(e0), .out1(e1), .out2(e2), .out3(e3), .out4(e4), .out5(e5), .out6(e6), .out7(e7), .out8(e8),
    .out9(e9), .out10(e10), .out11(e11), .out12(e12), .out13(e13), .out14(e14), .out15(e15), .out16(e16),
    .out17(e17), .out18(e18), .out19(e19), .out20(e20), .out21(e21), .out22(e22), .out23(e23), .out24(e24),
    .out25(e25), .out26(e26), .out27(e27), .out28(e28), .out29(e29), .out30(e30), .out31(e31), .sel(in_6),
    .en(in_7));
  Register #(.width(32)) R3 (.D(in_2), .en(e3), .Q(s3), .clk(in_4), .clr(in_5));
  Register #(.width(32)) R9 (.D(in_2), .en(e9), .Q(s9), .clk(in_4), .clr(in_5));
  Register #(.width(32)) R15 (.D(in_2), .en(e15), .Q(s15), .clk(in_4), .clr(in_5));
  Register #(.width(32)) R21 (.D(in_2), .en(e21), .Q(s21), .clk(in_4), .clr(in_5));
  Register #(.width(32)) R27 (.D(in_2), .en(e27), .Q(s27), .clk(in_4), .clr(in_5));
  Register #(.width(32)) R4 (.D(in_2), .en(e4), .Q(s4), .clk(in_4), .clr(in_5));
  Register #(.width(32)) R10 (.D(in_2), .en(e10), .Q(s10), .clk(in_4), .clr(in_5));
  Register #(.width(32)) R16 (.D(in_2), .en(e16), .Q(s16), .clk(in_4), .clr(in_5));
  Register #(.width(32)) R22 (.D(in_2), .en(e22), .Q(s22), .clk(in_4), .clr(in_5));
  Register #(.width(32)) R28 (.D(in_2), .en(e28), .Q(s28), .clk(in_4), .clr(in_5));
  Register #(.width(32)) R5 (.D(in_2), .en(e5), .Q(s5), .clk(in_4), .clr(in_5));
  Register #(.width(32)) R11 (.D(in_2), .en(e11), .Q(s11), .clk(in_4), .clr(in_5));
  Register #(.width(32)) R17 (.D(in_2), .en(e17), .Q(s17), .clk(in_4), .clr(in_5));
  Register #(.width(32)) R23 (.D(in_2), .en(e23), .Q(s23), .clk(in_4), .clr(in_5));
  Register #(.width(32)) R29 (.D(in_2), .en(e29), .Q(s29), .clk(in_4), .clr(in_5));
  Register #(.width(32)) R6 (.D(in_2), .en(e6), .Q(s6), .clk(in_4), .clr(in_5));
  Register #(.width(32)) R12 (.D(in_2), .en(e12), .Q(s12), .clk(in_4), .clr(in_5));
  Register #(.width(32)) R18 (.D(in_2), .en(e18), .Q(s18), .clk(in_4), .clr(in_5));
  Register #(.width(32)) R24 (.D(in_2), .en(e24), .Q(s24), .clk(in_4), .clr(in_5));
  Register #(.width(32)) R30 (.D(in_2), .en(e30), .Q(s30), .clk(in_4), .clr(in_5));
  Multiplexer #(.select(5), .width(32)) multiplexer_1 (
    .in0({32{1'b0}}), .in1(s1), .in2(s2), .in3(s3), .in4(s4), .in5(s5), .in6(s6), .in7(s7), .in8(s8),
    .in9(s9), .in10(s10), .in11(s11), .in12(s12), .in13(s13), .in14(s14), .in15(s15), .in16(s16), .in17(s17),
    .in18(s18), .in19(s19), .in20(s20), .in21(s21), .in22(s22), .in23(s23), .in24(s24), .in25(s25),
    .in26(s26), .in27(s27), .in28(s28), .in29(s29), .in30(s30), .in31(s31), .out(out_8), .sel(in_1));  // open: en
  Multiplexer #(.select(5), .width(32)) multiplexer_2 (
    .in0({32{1'b0}}), .in1(s1), .in2(s2), .in3(s3), .in4(s4), .in5(s5), .in6(s6), .in7(s7), .in8(s8),
    .in9(s9), .in10(s10), .in11(s11), .in12(s12), .in13(s13), .in14(s14), .in15(s15), .in16(s16), .in17(s17),
    .in18(s18), .in19(s19), .in20(s20), .in21(s21), .in22(s22), .in23(s23), .in24(s24), .in25(s25),
    .in26(s26), .in27(s27), .in28(s28), .in29(s29), .in30(s30), .in31(s31), .out(out_9), .sel(in_3));  // open: en

  // Other names for the same wires on the sheet: A[31:0] = out_8; B[31:0] = out_9; Clock = in_4; DA[4:0] = in_6;
  //   Inp[31:0] = in_2; Reset = in_5; RW = in_7; S_A[4:0] = in_1; S_B[4:0] = in_3

  // Notes on the sheet:
  //   R
  //   INPUT
  //   EGISTER
  //   F
  //   REGISTER
  //   WRITE SELECTION
  //   ILE
  //   OUTPUT
  //   OUTPUT SELECTION
endmodule
