// Logisim project s-mips.circ as structural Verilog
module S_MIPS_Board (
  input  DESHABILITAR_DISPATCHER,
  output halt
);

  wire button_1_out, CLK, CS, d_ff_1_q, LCLR, LoadRAM, LoadRAMOn, LW, R_R_W, R_W, ram_dispatcher_1_finished,
       RCS, Reset_out, RST, TTY_EN;
  wire [2:0] KDB;
  wire [3:0] LMask, Mask, ram_1_read_time, ram_1_write_time, RMask;
  wire [6:0] KDB_DATA, TTY_DATA;
  wire [15:0] Addr, LAddr, RAddr;
  wire [31:0] I0, I1, I2, I3, LData, ram_1_data_out_0, ram_1_data_out_1, ram_1_data_out_2, ram_1_data_out_3,
       RI0, RI1, RI2, RI3;

  TTY #(.rows(25), .cols(80)) tty_1 (.data(TTY_DATA), .clk(CLK), .we(TTY_EN), .clr(RST));
  not not_1 (LoadRAMOn, ram_dispatcher_1_finished);
  RAM_Dispatcher ram_dispatcher_1 (
    .WriteTime(ram_1_write_time), .Clock(CLK), .Data(LData), .Address(LAddr), .Mask(LMask),
    .Finished(ram_dispatcher_1_finished), .Write(LW), .CLR(LCLR));
  Keyboard #(.buflen(64)) keyboard_1 (.clk(CLK), .re(KDB[0]), .avail(KDB[2]), .data(KDB_DATA));  // open: clr
  RAM ram_1 (
    .Address(RAddr), .Data_Out_0(ram_1_data_out_0), .Data_Out_1(ram_1_data_out_1),
    .Data_Out_2(ram_1_data_out_2), .Data_Out_3(ram_1_data_out_3), .Data_In_0(RI0), .Data_In_1(RI1),
    .Data_In_2(RI2), .Data_In_3(RI3), .Mask(RMask), .nRead_Write(R_R_W), .Chip_Select(RCS),
    .Read_Time(ram_1_read_time), .Reset(button_1_out), .Write_Time(ram_1_write_time));
  Button button_1 (.out(button_1_out));
  D_Flip_Flop d_ff_1 (.clk(CLK), .D(1'b1), .Q(d_ff_1_q), .reset(Reset_out));  // open: Qn, preset, en
  Button Reset (.out(Reset_out));
  S_MIPS s_mips_1 (
    .Kbd_Enable(KDB[0]), .Address(Addr), .Kbd_Clear(KDB[1]), .Kbd_Available(KDB[2]), .RAM_In_0(I0),
    .Kbd_ASCII_Data(KDB_DATA), .RAM_In_1(I1), .TTY_Enable(TTY_EN), .RAM_In_2(I2), .RAM_In_3(I3),
    .TTY_ASCII_Data(TTY_DATA), .Reset(RST), .RAM_Out_0(ram_1_data_out_0), .Clock(CLK),
    .RAM_Out_1(ram_1_data_out_1), .Stop(halt), .RAM_Out_2(ram_1_data_out_2), .RAM_Out_3(ram_1_data_out_3),
    .Mask(Mask), .Read_Time(ram_1_read_time), .Write_Time(ram_1_write_time), .nRead_Write(R_W),
    .Chip_Select(CS));
  D_Flip_Flop d_ff_2 (.clk(CLK), .D(d_ff_1_q), .Qn(LCLR), .reset(Reset_out));  // open: Q, preset, en
  or or_1 (RST, LCLR, LoadRAM);
  Clock clock_1 (.out(CLK));
  Multiplexer #(.width(32), .enable("false")) multiplexer_1 (.in0(I0), .in1(LData), .out(RI0), .sel(LoadRAM));
  Multiplexer #(.width(32), .enable("false")) multiplexer_2 (.in0(I1), .in1(LData), .out(RI1), .sel(LoadRAM));
  Multiplexer #(.width(32), .enable("false")) multiplexer_3 (.in0(I2), .in1(LData), .out(RI2), .sel(LoadRAM));
  Multiplexer #(.width(32), .enable("false")) multiplexer_4 (.in0(I3), .in1(LData), .out(RI3), .sel(LoadRAM));
  and and_1 (LoadRAM, ~DESHABILITAR_DISPATCHER, LoadRAMOn);  // AND_Gate
  Multiplexer #(.width(16), .enable("false")) multiplexer_5 (.in0(Addr), .in1(LAddr), .out(RAddr), .sel(LoadRAM));
  Multiplexer #(.width(4), .enable("false")) multiplexer_6 (.in0(Mask), .in1(LMask), .out(RMask), .sel(LoadRAM));
  Multiplexer #(.enable("false")) multiplexer_7 (.in0(CS), .in1(LW), .out(RCS), .sel(LoadRAM));
  Multiplexer #(.enable("false")) multiplexer_8 (.in0(R_W), .in1(LW), .out(R_R_W), .sel(LoadRAM));

  // Notes on the sheet:
  //   NO MODIFICAR
  //   Keyboard
endmodule

module RAM (
  input  [15:0] Address,
  input  [31:0] Data_In_0,
  input  [31:0] Data_In_1,
  input  [31:0] Data_In_2,
  input  [31:0] Data_In_3,
  input  [3:0] Mask,
  input  nRead_Write,
  input  Chip_Select,
  input  Reset,
  output [31:0] Data_Out_0,
  output [31:0] Data_Out_1,
  output [31:0] Data_Out_2,
  output [31:0] Data_Out_3,
  output [3:0] Read_Time,
  output [3:0] Write_Time
);

  wire and_2_out, and_3_out, and_4_out, and_5_out, and_6_out, and_7_out, and_8_out, and_9_out, Changed, CLK,
       comparator_2_eq, comparator_3_eq, comparator_4_eq, comparator_5_eq, comparator_6_eq, Count,
       demultiplexer_3_out0, Idle, Idle_q, Load, Load0, Load1, nand_1_out, or_1_out, or_2_out, or_3_out,
       or_4_out, or_5_out, or_6_out, or_7_out, or_8_out, or_9_out, or_10_out, Proc_q, Update_Mem, Zero_Time;
  wire [3:0] counter_1_q, multiplexer_1_out, subtractor_1_out;
  wire [31:0] register_1_q, register_2_q, register_3_q, register_4_q, register_5_q;

  // Probe on 4'b0011
  // Probe on 4'b0010
  Multiplexer #(.width(4), .enable("false")) multiplexer_1 (
    .in0(4'b0011), .in1(4'b0010), .out(multiplexer_1_out), .sel(nRead_Write));
  or or_1 (or_1_out, Idle, Update_Mem);
  or or_2 (or_2_out, ~Chip_Select, Reset);  // OR_Gate
  Subtractor #(.width(4)) subtractor_1 (.a(multiplexer_1_out), .b(4'b0010), .out(subtractor_1_out));  // open: bin, bout
  D_Flip_Flop u_Idle (.clk(CLK), .D(or_1_out), .Q(Idle_q), .preset(or_2_out));  // open: Qn, en, reset
  Demultiplexer #(.enable("false")) demultiplexer_1 (.out0(Idle), .out1(Load0), .in(Idle_q), .sel(Changed));
  // Probe on counter_1_q
  Counter #(.width(4), .max('hf)) counter_1 (
    .load(Load), .D(subtractor_1_out), .count(Count), .Q(counter_1_q), .clk(CLK), .clr(or_3_out));  // open: carry
  or or_3 (or_3_out, ~Chip_Select, Reset);  // OR_Gate
  Comparator #(.width(4), .mode("unsigned")) comparator_1 (
    .a(4'b0000), .b(counter_1_q), .eq(Zero_Time));  // open: gt, lt
  or or_4 (or_4_out, Count, Load0, Load1);
  Register #(.width(32)) register_1 (.D(Data_In_0), .en(Chip_Select), .Q(register_1_q), .clk(CLK), .clr(or_5_out));
  or or_5 (or_5_out, ~Chip_Select, Reset);  // OR_Gate
  Register #(.width(32)) register_2 (.D(Data_In_1), .en(Chip_Select), .Q(register_2_q), .clk(CLK), .clr(or_6_out));
  or or_6 (or_6_out, ~Chip_Select, Reset);  // OR_Gate
  Register #(.width(32)) register_3 (.D(Data_In_2), .en(Chip_Select), .Q(register_3_q), .clk(CLK), .clr(or_7_out));
  or or_7 (or_7_out, ~Chip_Select, Reset);  // OR_Gate
  Register #(.width(32)) register_4 (.D(Data_In_3), .en(Chip_Select), .Q(register_4_q), .clk(CLK), .clr(or_8_out));
  or or_8 (or_8_out, ~Chip_Select, Reset);  // OR_Gate
  Register #(.width(32)) register_5 (
    .D({{11{1'b1}}, nRead_Write, Mask, Address}), .en(Chip_Select), .Q(register_5_q), .clk(CLK),
    .clr(or_9_out));
  or or_9 (or_9_out, ~Chip_Select, Reset);  // OR_Gate
  D_Flip_Flop Proc (.clk(CLK), .D(or_4_out), .Q(Proc_q), .reset(or_10_out));  // open: Qn, preset, en
  or or_10 (or_10_out, ~Chip_Select, Reset);  // OR_Gate
  Demultiplexer #(.enable("false")) demultiplexer_2 (
    .out0(Count), .out1(Update_Mem), .in(demultiplexer_3_out0), .sel(Zero_Time));
  Demultiplexer #(.enable("false")) demultiplexer_3 (
    .out0(demultiplexer_3_out0), .out1(Load1), .in(Proc_q), .sel(Changed));
  Clock clock_1 (.out(CLK));
  Comparator #(.width(32)) comparator_2 (.a(register_1_q), .b(Data_In_0), .eq(comparator_2_eq));  // open: gt, lt
  Comparator #(.width(32)) comparator_3 (.a(register_2_q), .b(Data_In_1), .eq(comparator_3_eq));  // open: gt, lt
  Comparator #(.width(32)) comparator_4 (.a(register_3_q), .b(Data_In_2), .eq(comparator_4_eq));  // open: gt, lt
  Comparator #(.width(32)) comparator_5 (.a(register_4_q), .b(Data_In_3), .eq(comparator_5_eq));  // open: gt, lt
  Comparator #(.width(32)) comparator_6 (
    .a(register_5_q), .b({{11{1'b1}}, nRead_Write, Mask, Address}), .eq(comparator_6_eq));  // open: gt, lt
  nand nand_1 (nand_1_out, comparator_6_eq, comparator_2_eq, comparator_3_eq, comparator_4_eq, comparator_5_eq);
  and and_1 (Changed, nand_1_out, Chip_Select);
  or or_11 (Load, Count, Load1, Load0);
  and and_2 (and_2_out, Mask[0], Update_Mem, nRead_Write);
  and and_3 (and_3_out, Mask[1], Update_Mem, nRead_Write);
  and and_4 (and_4_out, Mask[2], Update_Mem, nRead_Write);
  and and_5 (and_5_out, Mask[3], Update_Mem, nRead_Write);
  RAM_part #(.addrWidth(16), .dataWidth(32), .bus("separate")) ram_1 (
    .addr(Address), .din(Data_In_0), .data(Data_Out_0), .str(and_2_out), .sel(Chip_Select), .clk(CLK),
    .ld(and_6_out), .clr(Reset));
  and and_6 (and_6_out, ~nRead_Write, Idle);  // AND_Gate
  RAM_part #(.addrWidth(16), .dataWidth(32), .bus("separate")) ram_2 (
    .addr(Address), .din(Data_In_1), .data(Data_Out_1), .str(and_3_out), .sel(Chip_Select), .clk(CLK),
    .ld(and_7_out), .clr(Reset));
  and and_7 (and_7_out, ~nRead_Write, Idle);  // AND_Gate
  RAM_part #(.addrWidth(16), .dataWidth(32), .bus("separate")) ram_3 (
    .addr(Address), .din(Data_In_2), .data(Data_Out_2), .str(and_4_out), .sel(Chip_Select), .clk(CLK),
    .ld(and_8_out), .clr(Reset));
  and and_8 (and_8_out, ~nRead_Write, Idle);  // AND_Gate
  RAM_part #(.addrWidth(16), .dataWidth(32), .bus("separate")) ram_4 (
    .addr(Address), .din(Data_In_3), .data(Data_Out_3), .str(and_5_out), .sel(Chip_Select), .clk(CLK),
    .ld(and_9_out), .clr(Reset));
  and and_9 (and_9_out, ~nRead_Write, Idle);  // AND_Gate

  assign Read_Time = 4'b0011;
  assign Write_Time = 4'b0010;

  // Other names for the same wires on the sheet: M0 = Mask[0]; M1 = Mask[1]; M2 = Mask[2]; M3 = Mask[3];
  //   RW = nRead_Write; CLR = Reset; CS = Chip_Select; Load2 = Count

  // Notes on the sheet:
  //   NO MODIFICAR
  //   excepto quizás los valores RT y WT
  //   BANK0
  //   BANK1
  //   BANK2
  //   BANK3
endmodule

module S_MIPS (
  input  Kbd_Available,
  input  [6:0] Kbd_ASCII_Data,
  input  [31:0] RAM_Out_0,
  input  [31:0] RAM_Out_1,
  input  Reset,
  input  [31:0] RAM_Out_2,
  input  Clock,
  input  [31:0] RAM_Out_3,
  input  [3:0] Read_Time,
  input  [3:0] Write_Time,
  output Kbd_Enable,
  output [15:0] Address,
  output Kbd_Clear,
  output TTY_Enable,
  output [6:0] TTY_ASCII_Data,
  output Stop,
  output [31:0] RAM_In_0,
  output [31:0] RAM_In_1,
  output [31:0] RAM_In_2,
  output [31:0] RAM_In_3,
  output [3:0] Mask,
  output nRead_Write,
  output Chip_Select
);


  // Other names for the same wires on the sheet: CLK = Clock; CLR = Reset; CS = Chip_Select;
  //   KBD_AVAIL = Kbd_Available; KBD_CLR = Kbd_Clear; KBD_DATA[6:0] = Kbd_ASCII_Data; RAM_A[15:0] = Address;
  //   RAM_INPUT_0[31:0] = RAM_In_0; RAM_INPUT_1[31:0] = RAM_In_1; RAM_INPUT_2[31:0] = RAM_In_2;
  //   RAM_INPUT_3[31:0] = RAM_In_3; RAM_MASK[3:0] = Mask; RAM_OUTPUT_0[31:0] = RAM_Out_0;
  //   RAM_OUTPUT_1[31:0] = RAM_Out_1; RAM_OUTPUT_2[31:0] = RAM_Out_2; RAM_OUTPUT_3[31:0] = RAM_Out_3;
  //   RW = nRead_Write; TTY_DATA[6:0] = TTY_ASCII_Data

  // Notes on the sheet:
  //   RAM ADDRESS
  //   DATA FROM RAM
  //   DATA TO RAM
  //   DATA WRITE MASK
  //   RAM TIMING
  //   RAM CONTROL
  //   KEYBOARD
  //   TTY
  //   SEQUENCING
endmodule

module RAM_Dispatcher (
  input  [3:0] WriteTime,
  input  Clock,
  input  CLR,
  output [31:0] Data,
  output [15:0] Address,
  output [3:0] Mask,
  output Finished,
  output Write
);

  wire demultiplexer_2_out1, demultiplexer_3_out1, End, IDLE_q, IncAddr, Load, or_1_out, or_2_out, While_q,
       WriteEnd;
  wire [3:0] counter_1_q;
  wire [31:0] CurrentAddress_q;

  Counter #(.width(32), .max('hffffffff)) CurrentAddress (
    .count(IncAddr), .Q({CurrentAddress_q[31:18], Address, CurrentAddress_q[1:0]}), .clk(Clock), .clr(CLR));  // open: load, D, carry
  or or_1 (or_1_out, IncAddr, demultiplexer_3_out1, Finished);
  D_Flip_Flop IDLE (.clk(Clock), .D(or_1_out), .Q(IDLE_q), .preset(CLR));  // open: Qn, en, reset
  Demultiplexer #(.enable("false")) demultiplexer_1 (.out0(Load), .out1(Finished), .in(IDLE_q), .sel(End));
  D_Flip_Flop While (.clk(Clock), .D(or_2_out), .Q(While_q), .reset(CLR));  // open: Qn, preset, en
  or or_2 (or_2_out, Write, Load);
  RAM_part #(.addrWidth(18), .dataWidth(32)) ram_1 (
    .addr({Address, CurrentAddress_q[1:0]}), .data(Data), .clk(Clock));  // open: sel, ld, clr
  Demultiplexer #(.enable("false")) demultiplexer_2 (
    .out0(Write), .out1(demultiplexer_2_out1), .in(While_q), .sel(WriteEnd));
  Decoder #(.select(2)) decoder_1 (
    .out0(Mask[0]), .out1(Mask[1]), .out2(Mask[2]), .out3(Mask[3]), .sel(CurrentAddress_q[1:0]));  // open: en
  Demultiplexer #(.enable("false")) demultiplexer_3 (
    .out0(IncAddr), .out1(demultiplexer_3_out1), .in(demultiplexer_2_out1), .sel(End));
  Counter #(.width(4), .max('hf)) counter_1 (
    .load(Load), .D(WriteTime), .count(Write), .Q(counter_1_q), .clk(Clock));  // open: carry, clr
  Comparator #(.width(32)) comparator_1 (.a(Data), .b({32{1'b1}}), .eq(End));  // open: gt, lt
  Comparator #(.width(4)) comparator_2 (.a(4'b0000), .b(counter_1_q), .eq(WriteEnd));  // open: gt, lt

  // Other names for the same wires on the sheet: CLK = Clock; Count = Write; WT[3:0] = WriteTime
endmodule

module Register_File (
  input  [4:0] INPUT,
  input  [31:0] in_2,
  input  [4:0] in_3,
  input  [31:0] in_4,
  input  [31:0] in_5,
  input  in_6,
  input  in_7,
  input  [4:0] in_8,
  input  in_9,
  input  in_10,
  input  in_11,
  output [31:0] out_12,
  output [31:0] out_13,
  output [31:0] out_14
);

  wire e0, e1, e2, e3, e4, e5, e6, e7, e8, e9, e10, e11, e12, e13, e14, e15, e16, e17, e18, e19, e20, e21,
       e22, e23, e24, e25, e26, e27, e28, e29, e30, e31;
  wire [31:0] Hi, Lo, s1, s2, s3, s4, s5, s6, s7, s8, s9, s10, s11, s12, s13, s14, s15, s16, s17, s18, s19,
       s20, s21, s22, s23, s24, s25, s26, s27, s28, s29, s30, s31;

  Register #(.width(32)) R1 (.D(in_2), .en(e1), .Q(s1), .clk(in_6), .clr(in_7));
  Register #(.width(32)) R7 (.D(in_2), .en(e7), .Q(s7), .clk(in_6), .clr(in_7));
  Register #(.width(32)) R13 (.D(in_2), .en(e13), .Q(s13), .clk(in_6), .clr(in_7));
  Register #(.width(32)) R19 (.D(in_2), .en(e19), .Q(s19), .clk(in_6), .clr(in_7));
  Register #(.width(32)) R25 (.D(in_2), .en(e25), .Q(s25), .clk(in_6), .clr(in_7));
  Register #(.width(32)) R31 (.D(in_2), .en(e31), .Q(s31), .clk(in_6), .clr(in_7));
  Register #(.width(32)) R2 (.D(in_2), .en(e2), .Q(s2), .clk(in_6), .clr(in_7));
  Register #(.width(32)) R8 (.D(in_2), .en(e8), .Q(s8), .clk(in_6), .clr(in_7));
  Register #(.width(32)) R14 (.D(in_2), .en(e14), .Q(s14), .clk(in_6), .clr(in_7));
  Register #(.width(32)) R20 (.D(in_2), .en(e20), .Q(s20), .clk(in_6), .clr(in_7));
  Register #(.width(32)) R26 (.D(in_2), .en(e26), .Q(s26), .clk(in_6), .clr(in_7));
  Register #(.width(32)) u_Hi (.D(in_4), .en(in_10), .Q(Hi), .clk(in_6), .clr(in_7));
  Register #(.width(32)) R3 (.D(in_2), .en(e3), .Q(s3), .clk(in_6), .clr(in_7));
  Register #(.width(32)) R9 (.D(in_2), .en(e9), .Q(s9), .clk(in_6), .clr(in_7));
  Register #(.width(32)) R15 (.D(in_2), .en(e15), .Q(s15), .clk(in_6), .clr(in_7));
  Register #(.width(32)) R21 (.D(in_2), .en(e21), .Q(s21), .clk(in_6), .clr(in_7));
  Register #(.width(32)) R27 (.D(in_2), .en(e27), .Q(s27), .clk(in_6), .clr(in_7));
  Register #(.width(32)) u_Lo (.D(in_5), .en(in_10), .Q(Lo), .clk(in_6), .clr(in_7));
  Register #(.width(32)) R4 (.D(in_2), .en(e4), .Q(s4), .clk(in_6), .clr(in_7));
  Register #(.width(32)) R10 (.D(in_2), .en(e10), .Q(s10), .clk(in_6), .clr(in_7));
  Register #(.width(32)) R16 (.D(in_2), .en(e16), .Q(s16), .clk(in_6), .clr(in_7));
  Register #(.width(32)) R22 (.D(in_2), .en(e22), .Q(s22), .clk(in_6), .clr(in_7));
  Register #(.width(32)) R28 (.D(in_2), .en(e28), .Q(s28), .clk(in_6), .clr(in_7));
  Register #(.width(32)) R5 (.D(in_2), .en(e5), .Q(s5), .clk(in_6), .clr(in_7));
  Register #(.width(32)) R11 (.D(in_2), .en(e11), .Q(s11), .clk(in_6), .clr(in_7));
  Register #(.width(32)) R17 (.D(in_2), .en(e17), .Q(s17), .clk(in_6), .clr(in_7));
  Register #(.width(32)) R23 (.D(in_2), .en(e23), .Q(s23), .clk(in_6), .clr(in_7));
  Register #(.width(32)) R29 (.D(in_2), .en(e29), .Q(s29), .clk(in_6), .clr(in_7));
  Multiplexer #(.width(32), .enable("false")) multiplexer_1 (.in0(Hi), .in1(Lo), .out(out_12), .sel(in_11));
  Register #(.width(32)) R6 (.D(in_2), .en(e6), .Q(s6), .clk(in_6), .clr(in_7));
  Register #(.width(32)) R12 (.D(in_2), .en(e12), .Q(s12), .clk(in_6), .clr(in_7));
  Register #(.width(32)) R18 (.D(in_2), .en(e18), .Q(s18), .clk(in_6), .clr(in_7));
  Register #(.width(32)) R24 (.D(in_2), .en(e24), .Q(s24), .clk(in_6), .clr(in_7));
  Register #(.width(32)) R30 (.D(in_2), .en(e30), .Q(s30), .clk(in_6), .clr(in_7));
  Decoder #(.select(5)) decoder_1 (
    .out0(e0), .out1(e1), .out2(e2), .out3(e3), .out4(e4), .out5(e5), .out6(e6), .out7(e7), .out8(e8),
    .out9(e9), .out10(e10), .out11(e11), .out12(e12), .out13(e13), .out14(e14), .out15(e15), .out16(e16),
    .out17(e17), .out18(e18), .out19(e19), .out20(e20), .out21(e21), .out22(e22), .out23(e23), .out24(e24),
    .out25(e25), .out26(e26), .out27(e27), .out28(e28), .out29(e29), .out30(e30), .out31(e31), .sel(in_8),
    .en(in_9));
  Multiplexer #(.select(5), .width(32), .enable("false")) multiplexer_2 (
    .in0({32{1'b0}}), .in1(s1), .in2(s2), .in3(s3), .in4(s4), .in5(s5), .in6(s6), .in7(s7), .in8(s8),
    .in9(s9), .in10(s10), .in11(s11), .in12(s12), .in13(s13), .in14(s14), .in15(s15), .in16(s16), .in17(s17),
    .in18(s18), .in19(s19), .in20(s20), .in21(s21), .in22(s22), .in23(s23), .in24(s24), .in25(s25),
    .in26(s26), .in27(s27), .in28(s28), .in29(s29), .in30(s30), .in31(s31), .out(out_13), .sel(INPUT));
  Multiplexer #(.select(5), .width(32), .enable("false")) multiplexer_3 (
    .in0({32{1'b0}}), .in1(s1), .in2(s2), .in3(s3), .in4(s4), .in5(s5), .in6(s6), .in7(s7), .in8(s8),
    .in9(s9), .in10(s10), .in11(s11), .in12(s12), .in13(s13), .in14(s14), .in15(s15), .in16(s16), .in17(s17),
    .in18(s18), .in19(s19), .in20(s20), .in21(s21), .in22(s22), .in23(s23), .in24(s24), .in25(s25),
    .in26(s26), .in27(s27), .in28(s28), .in29(s29), .in30(s30), .in31(s31), .out(out_14), .sel(in_3));

  // Other names for the same wires on the sheet: A[31:0] = out_13; B[31:0] = out_14; Clock = in_6; DW[4:0] = in_8;
  //   H[31:0] = in_4; Inp[31:0] = in_2; L[31:0] = in_5; L___H[31:0] = out_12; L___H_R_W = in_10; L_H = in_11;
  //   R_W = in_9; Reset = in_7; S_A[4:0] = INPUT; S_B[4:0] = in_3

  // Notes on the sheet:
  //   Hi
  //   REGISTER
  //   Special Registers
  //   Lo
  //   R
  //   EGISTER
  //   F
  //   ILE
  //   OUTPUT SELECTION
  //   WRITE SELECTION
  //   OUTPUT
endmodule

module ALU (
  input  [31:0] in_1,
  input  [31:0] in_2,
  input  [3:0] in_3,
  output [31:0] out_4,
  output [31:0] out_5,
  output out_6,
  output out_7
);

  wire comparator_1_lt, comparator_2_lt, En;
  wire [31:0] AND, COMP, COMP_U, D_C, D_CU, DIV, DIV_U, M_C, M_CU, MUL, MUL_U, NOR, OR, SUB, SUM, XOR;

  Adder #(.width(32)) adder_1 (.a(in_1), .b(in_2), .out(SUM));  // open: cin, cout
  Divider_U_S divider_u_s_1 (.in_1(in_1), .in_2(in_2), .out_3(DIV), .out_4(D_C));
  Comparator #(.width(32)) comparator_1 (.a(in_1), .b(in_2), .lt(comparator_1_lt));  // open: gt, eq
  assign COMP = {{31{1'b0}}, comparator_1_lt};  // Bit_Extender bit_extender_1
  Multiplexer #(.select(2), .width(32)) multiplexer_1 (
    .in0(M_C), .in1(D_C), .in2(M_CU), .in3(D_CU), .out(out_5), .sel(in_3[1:0]), .en(En));
  nor nor_1 (En, in_3[2], in_3[3]);
  Subtractor #(.width(32)) subtractor_1 (.a(in_1), .b(in_2), .out(SUB));  // open: bin, bout
  Comparator #(.width(32), .mode("unsigned")) comparator_2 (.a(in_1), .b(in_2), .lt(comparator_2_lt));  // open: gt, eq
  Multiplier_S multiplier_s_1 (.in_1(in_1), .in_2(in_2), .out_3(MUL), .out_4(M_C));
  assign COMP_U = {{31{1'b0}}, comparator_2_lt};  // Bit_Extender bit_extender_2
  Multiplexer #(.select(4), .width(32), .enable("false")) multiplexer_2 (
    .in0(MUL), .in1(MUL_U), .in2(DIV), .in3(DIV_U), .in4(AND), .in5(SUB), .in6(XOR), .in7(SUM), .in8(OR),
    .in9(COMP_U), .in10(NOR), .in11(COMP), .out(out_4), .sel(in_3));  // open: in12, in13, in14, in15
  Comparator #(.width(32)) comparator_3 (.a(out_4), .b({32{1'b0}}), .eq(out_6), .lt(out_7));  // open: gt
  assign AND = in_1 & in_2;  // AND_Gate and_1, 32 bits wide
  Multiplier #(.width(32)) multiplier_1 (.a(in_1), .b(in_2), .out(MUL_U), .cout(M_CU));  // open: cin
  assign XOR = in_1 ^ in_2;  // XOR_Gate xor_1, 32 bits wide
  assign OR = in_1 | in_2;  // OR_Gate or_1, 32 bits wide
  Divider #(.width(32)) divider_1 (.a(in_1), .b(in_2), .out(DIV_U), .rem(D_CU));  // open: upper
  assign NOR = ~(in_1 | in_2);  // NOR_Gate nor_2, 32 bits wide

  // Other names for the same wires on the sheet: A[31:0] = in_1; B[31:0] = in_2; Carry[31:0] = out_5; N_flag = out_7;
  //   OP[3:0] = in_3; S_C[1:0] = in_3[1:0]; S[31:0] = out_4; ZERO_flag = out_6

  // Notes on the sheet:
  //   INPUT
  //   OPERACIONES
  //   SUMA
  //   DIVISIÓN
  //   COMPARADOR
  //   Aritmetic
  //   Carry
  //   -
  //   RESTA
  //   MULTIPLICACIÓN
  //   COMPARADOR U
  //   Logic
  //   Unit
  //   AND LOGIC
  //   MULTIPLICACIÓN U
  //   XOR
  //   (ALU)
  //   OR LOGIC
  //   DIVISIÓN U
  //   NOR
  //   OUTPUT
endmodule

module Instruction_Decoder (
  input  [31:0] in_1,
  output [25:0] out_2,
  output [4:0] out_3,
  output [4:0] out_4,
  output [4:0] out_5,
  output [15:0] out_6,
  output [3:0] out_7,
  output out_8,
  output out_9,
  output out_10,
  output out_11,
  output out_12,
  output out_13,
  output [2:0] out_14,
  output out_15,
  output out_16,
  output [1:0] out_17,
  output [2:0] out_18,
  output [1:0] out_19
);

  wire Addi, ALU, and_13_out, and_19_out, and_20_out, and_21_out, and_22_out, and_23_out, and_24_out,
       and_25_out, and_26_out, and_27_out, and_28_out, and_31_out, Andi, B_Comp_0, Beq, Bgtz, Blez, Bltz,
       Bne, Halt, I_Type_ALU, I_Type_Branch, I_Type_L_S, I_Type_t, J_Type, Jr, Kbd, N, Nop, Op_Log, or_6_out,
       or_8_out, Ori, R_Type_1, R_Type_ALU, R_Type_S, Rnd, Slt, Slti, Tty, tunnel, Xori;

  Multiplexer #(.width(3), .enable("false")) multiplexer_1 (.in0(in_1[28:26]), .in1(in_1[2:0]), .out(out_14), .sel(Jr));
  or or_1 (out_17[0], I_Type_L_S, B_Comp_0, I_Type_ALU);
  or or_2 (out_17[1], out_11, Addi, Slti);
  and and_1 (R_Type_ALU, R_Type_1, ~Nop, ~Jr);  // AND_Gate
  and and_2 (R_Type_1, ~in_1[26], ~in_1[27], ~in_1[28], ~in_1[29], ~in_1[30], ~in_1[31]);  // AND_Gate
  and and_3 (out_16, R_Type_ALU, in_1[3], in_1[4], ~in_1[5]);  // AND_Gate
  and and_4 (Op_Log, R_Type_ALU, ~out_12, ~Slt, ~tunnel, ~out_16);  // AND_Gate
  or or_3 (out_8, Jr, I_Type_Branch, J_Type);
  or or_4 (out_19[0], Tty, Kbd);
  or or_5 (out_19[1], Rnd, Kbd);
  and and_5 (Nop, R_Type_1, ~in_1[0], ~in_1[1], ~in_1[2], ~in_1[3], ~in_1[4], ~in_1[5]);  // AND_Gate
  and and_6 (tunnel, R_Type_ALU, ~in_1[2], ~in_1[3], ~in_1[4], in_1[5]);  // AND_Gate
  and and_7 (out_12, R_Type_ALU, ~in_1[2], ~in_1[3], in_1[4], ~in_1[5]);  // AND_Gate
  and and_8 (out_11, ~in_1[26], ~in_1[27], ~in_1[28], in_1[29], in_1[30], in_1[31]);  // AND_Gate
  and and_9 (out_10, out_11, ~in_1[0]);  // AND_Gate
  and and_10 (Jr, R_Type_1, ~in_1[0], ~in_1[1], ~in_1[2], in_1[3], ~in_1[4], ~in_1[5]);  // AND_Gate
  and and_11 (Slt, R_Type_ALU, in_1[1], ~in_1[2], in_1[3], ~in_1[4], in_1[5]);  // AND_Gate
  and and_12 (out_13, out_12, in_1[1]);
  and and_13 (and_13_out, Slti, ~in_1[26]);  // AND_Gate
  and and_14 (R_Type_S, in_1[26], in_1[27], in_1[28], in_1[29], in_1[30], in_1[31]);
  and and_15 (Halt, R_Type_S, in_1[0], in_1[1], in_1[2]);
  and and_16 (Tty, R_Type_S, in_1[0], ~in_1[1], ~in_1[2]);  // AND_Gate
  and and_17 (Rnd, R_Type_S, ~in_1[0], in_1[1], ~in_1[2]);  // AND_Gate
  and and_18 (Kbd, R_Type_S, ~in_1[0], ~in_1[1], in_1[2]);  // AND_Gate
  and and_19 (and_19_out, out_16, in_1[0]);
  and and_20 (and_20_out, out_16, in_1[1]);
  and and_21 (and_21_out, Slt, ~in_1[0]);  // AND_Gate
  or or_6 (or_6_out, in_1[1], ~in_1[2]);  // OR_Gate
  and and_22 (and_22_out, in_1[2], ~in_1[0], ~in_1[1]);  // AND_Gate
  and and_23 (and_23_out, I_Type_Branch, ~in_1[27], in_1[28]);  // AND_Gate
  and and_24 (and_24_out, tunnel, ~in_1[1]);  // AND_Gate
  or or_7 (out_7[1], and_13_out, and_20_out, Addi, and_24_out, I_Type_L_S, Xori, out_10, and_21_out, and_25_out);
  and and_25 (and_25_out, Op_Log, or_6_out);
  or or_8 (or_8_out, and_22_out, ~in_1[2]);  // OR_Gate
  and and_26 (and_26_out, Op_Log, in_1[0]);
  Priority_Encoder priority_encoder_1 (
    .in0(N), .in1(ALU), .in2(I_Type_L_S), .in3(out_11), .in4(R_Type_S), .in5(I_Type_Branch), .out(out_18));  // open: in6, in7, en_in, gs, en_out
  and and_27 (and_27_out, I_Type_Branch, ~in_1[27], in_1[28]);  // AND_Gate
  and and_28 (and_28_out, Op_Log, or_8_out);
  or or_9 (out_7[3], Ori, Slti, B_Comp_0, Slt, and_26_out, out_12);
  or or_10 (out_7[0], and_19_out, and_23_out, Slti, Slt, tunnel, Addi, out_11, I_Type_L_S);
  or or_11 (out_7[2], and_27_out, out_12, Addi, Andi, out_11, and_28_out, Xori, B_Comp_0, tunnel, I_Type_L_S);
  and and_29 (out_15, ~R_Type_1, ~R_Type_S, ~out_11, ~J_Type);  // AND_Gate
  and and_30 (I_Type_Branch, I_Type_t, ~in_1[29], ~in_1[30], ~in_1[31]);  // AND_Gate
  and and_31 (and_31_out, ~in_1[27], in_1[28]);  // AND_Gate
  or or_12 (ALU, R_Type_ALU, I_Type_ALU);
  or or_13 (N, J_Type, Nop, Jr);
  and and_32 (Beq, I_Type_Branch, ~in_1[26], ~in_1[27], ~in_1[28]);  // AND_Gate
  and and_33 (Bne, I_Type_Branch, ~in_1[26], ~in_1[27], ~in_1[28]);  // AND_Gate
  and and_34 (Blez, I_Type_Branch, ~in_1[26], ~in_1[27], ~in_1[28]);  // AND_Gate
  and and_35 (Bgtz, I_Type_Branch, ~in_1[26], ~in_1[27], ~in_1[28]);  // AND_Gate
  and and_36 (Bltz, I_Type_Branch, ~in_1[26], ~in_1[27], ~in_1[28]);  // AND_Gate
  and and_37 (B_Comp_0, I_Type_Branch, ~and_31_out);  // AND_Gate
  and and_38 (I_Type_L_S, out_15, ~I_Type_Branch, ~I_Type_ALU);  // AND_Gate
  and and_39 (out_9, ~in_1[29], I_Type_L_S);  // AND_Gate
  and and_40 (I_Type_ALU, I_Type_t, in_1[29], ~in_1[30], ~in_1[31]);  // AND_Gate
  and and_41 (Addi, I_Type_ALU, ~in_1[26], ~in_1[27], ~in_1[28]);  // AND_Gate
  and and_42 (Andi, I_Type_ALU, ~in_1[26], ~in_1[27], in_1[28]);  // AND_Gate
  and and_43 (Ori, I_Type_ALU, in_1[26], ~in_1[27], in_1[28]);  // AND_Gate
  and and_44 (Xori, I_Type_ALU, ~in_1[26], in_1[27], in_1[28]);  // AND_Gate
  and and_45 (Slti, I_Type_ALU, ~in_1[26], in_1[27], ~in_1[28]);  // AND_Gate
  and and_46 (J_Type, ~in_1[26], in_1[27], ~in_1[28], ~in_1[29], ~in_1[30], ~in_1[31]);  // AND_Gate

  assign out_2 = in_1[25:0];
  assign out_3 = in_1[25:21];
  assign out_4 = in_1[20:16];
  assign out_5 = in_1[15:11];
  assign out_6 = in_1[15:0];

  // Other names for the same wires on the sheet: Branch_Code[2:0] = out_14; I_Type = out_15; Const[15:0] = in_1[15:0];
  //   Destino_Salto[25:0] = in_1[25:0]; F0 = in_1[0]; Func_Code[5:0] = in_1[5:0]; Inst[31:0] = in_1; F1 = in_1[1];
  //   F2 = in_1[2]; F3 = in_1[3]; F4 = in_1[4]; F5 = in_1[5]; X[4:0] = in_1[10:6]; Rd[4:0] = in_1[15:11];
  //   Rt[4:0] = in_1[20:16]; Rs[4:0] = in_1[25:21]; O0 = in_1[26]; Op_Code[5:0] = in_1[31:26]; O1 = in_1[27];
  //   O2 = in_1[28]; O3 = in_1[29]; O4 = in_1[30]; O5 = in_1[31]; Jump = out_8; Load = out_9; M_D = out_16;
  //   mflo = out_13; Move = out_12; OP_ALU[3:0] = out_7; Op_CU[2:0] = out_18; Pop = out_10; R_Type_PP = out_11;
  //   S_B[1:0] = out_17; Special_OP[1:0] = out_19

  // Notes on the sheet:
  //   INPUT
  //   OUTPUT
  //   Flags
  //   Branch
  //   Sel-B
  //   R-Type ALU
  //   R-Type Basic
  //   Jump
  //   R-Type
  //   R-Type Pop/Push
  //   Instruction Decoder
  //   R-Type S
  //   OP ALU
  //   I-Type
  //   I-Type Jump
  //   I-Type Load/Store
  //   I-Type ALU
  //   J-Type
endmodule

module Branch_Control (
  input  [25:0] in_1,
  input  [31:0] in_2,
  input  [31:0] in_3,
  input  [31:0] in_4,
  input  in_5,
  input  in_6,
  input  in_7,
  input  [2:0] in_8,
  output [31:0] out_9
);

  wire and_1_out, and_2_out, and_3_out, and_4_out, and_5_out, and_6_out, BGTZ_out;
  wire [1:0] S_Salto;
  wire [31:0] I_Type, Next, shifter_1_out;

  and and_1 (and_1_out, in_5, ~in_8[0], ~in_8[1], ~in_8[2]);  // AND_Gate
  and and_2 (and_2_out, ~in_8[0], in_8[2], ~in_6, in_7, in_5);  // AND_Gate
  or or_1 (S_Salto[1], and_1_out, and_3_out);
  and and_3 (and_3_out, ~in_8[0], in_8[1], ~in_8[2], in_5);  // AND_Gate
  and and_4 (and_4_out, in_8[0], ~in_8[1], in_6, ~in_7, in_5);  // AND_Gate
  Adder #(.width(32)) adder_1 (.a(in_2), .b(32'h4), .out(Next));  // open: cin, cout
  and BGTZ (BGTZ_out, in_8[0], in_8[1], in_8[2], ~in_6, ~in_7, in_5);  // AND_Gate
  and and_5 (and_5_out, ~in_8[0], in_8[1], in_6, ~in_7, in_5);  // AND_Gate
  Shifter #(.width(32)) shifter_1 (.in(in_3), .\dist (5'b00010), .out(shifter_1_out));
  or or_2 (S_Salto[0], and_3_out, BGTZ_out, and_2_out, and_4_out, and_5_out, and_6_out);
  Multiplexer #(.select(2), .width(32), .enable("false")) multiplexer_1 (
    .in0(Next), .in1(I_Type), .in2(in_4), .in3({in_2[31:28], in_1, 2'b00}), .out(out_9), .sel(S_Salto));
  Adder #(.width(32)) adder_2 (.a(shifter_1_out), .b(Next), .out(I_Type));  // open: cin, cout
  and and_6 (and_6_out, in_8[0], ~in_8[1], ~in_7, in_5);  // AND_Gate

  // Other names for the same wires on the sheet: B0 = in_8[0]; Branch_Code[2:0] = in_8; B1 = in_8[1]; B2 = in_8[2];
  //   D_S[31:2] = {in_2[31:28], in_1}; Destino_Salto[25:0] = in_1; Complement[3:0] = in_2[31:28]; PC[31:0] = in_2;
  //   Jr[31:0] = in_4; Jump = in_5; N = in_6; Off[31:0] = in_3; PC_new[31:0] = out_9; Z = in_7

  // Notes on the sheet:
  //   Input
  //   Selector
  //   Next 
  //   Branch Control
  //   Output
  //   I-Type
  //   J-Type
endmodule

module Data_Path (
  input  Input,
  input  in_2,
  input  in_3,
  input  [31:0] in_4,
  input  [3:0] in_5,
  input  [1:0] in_6,
  input  [31:0] in_7,
  input  in_8,
  input  in_9,
  input  [1:0] in_10,
  input  [31:0] in_11,
  input  [31:0] in_12,
  input  [31:0] in_13,
  output [31:0] out_14,
  output [15:0] out_15,
  output [3:0] out_16,
  output out_17,
  output out_18,
  output [31:0] out_19,
  output out_20,
  output [1:0] out_21,
  output [1:0] out_22,
  output out_23,
  output out_24,
  output [2:0] out_25
);

  wire Jump, L_H_R_W, Load, M_D, mflo, Move, N, Pop, R_Type_PP, R_W_RF, Z;
  wire [1:0] S_B, S_Op;
  wire [2:0] B_C, Op_CU;
  wire [3:0] Op_ALU;
  wire [4:0] DW, Rd, Rs, Rt, S_S_B;
  wire [15:0] Cte;
  wire [25:0] D_S;
  wire [31:0] A, A_ALU, B, B_ALU, Cte_Ext, H_L, Hi, Inp, Instruction, M_I, multiplexer_1_out,
       multiplexer_2_out, Out, PC, PC_star, random_1_out, Z_Cte_Ext;

  Register #(.width(32)) u_PC (.D(PC_star), .en(in_3), .Q(PC), .clk(Input), .clr(in_2));
  Multiplexer #(.width(32), .enable("false")) multiplexer_1 (
    .in0(PC), .in1(Out), .out(multiplexer_1_out));  // open: sel
  ALU alu_1 (.in_1(A_ALU), .in_3(Op_ALU), .in_2(B_ALU), .out_4(Out), .out_5(Hi), .out_6(Z), .out_7(N));
  Multiplexer #(.width(32), .enable("false")) multiplexer_2 (
    .in0(A), .in1(B), .out(multiplexer_2_out), .sel(R_Type_PP));
  Instruction_Memory instruction_memory_1 (
    .in_1(in_4), .in_2(in_11), .in_3(in_7), .in_4(in_12), .Address(multiplexer_1_out), .in_6(B),
    .out_7(Instruction), .out_8(out_14), .Address_2(out_15), .MASK(out_16));
  Multiplexer #(.select(2), .width(32), .enable("false")) multiplexer_3 (
    .in0(B), .in1(Z_Cte_Ext), .in2(32'h4), .in3(Cte_Ext), .out(B_ALU), .sel(S_B));
  Branch_Control branch_control_1 (
    .in_1(D_S), .in_2(PC), .in_3(Cte_Ext), .in_4(A), .in_5(Jump), .in_6(N), .in_7(Z), .in_8(B_C),
    .out_9(PC_star));
  Multiplexer #(.width(32), .enable("false")) multiplexer_4 (
    .in0(multiplexer_2_out), .in1(H_L), .out(A_ALU), .sel(Move));
  Instruction_Decoder instruction_decoder_1 (
    .in_1(Instruction), .out_2(D_S), .out_3(Rs), .out_4(Rt), .out_5(Rd), .out_6(Cte), .out_7(Op_ALU),
    .out_8(Jump), .out_9(Load), .out_10(Pop), .out_11(R_Type_PP), .out_12(Move), .out_13(mflo), .out_14(B_C),
    .out_15(out_20), .out_16(M_D), .out_17(S_B), .out_18(Op_CU), .out_19(S_Op));
  assign Cte_Ext = {{16{Cte[15]}}, Cte};  // Bit_Extender bit_extender_1
  assign Z_Cte_Ext = {{16{1'b0}}, Cte};  // Bit_Extender bit_extender_2
  Register_File register_file_1 (
    .INPUT(Rs), .in_2(Inp), .in_3(S_S_B), .in_4(Hi), .in_5(Out), .in_6(Input), .in_7(in_2), .in_8(DW),
    .in_9(R_W_RF), .in_10(L_H_R_W), .in_11(mflo), .out_12(H_L), .out_13(A), .out_14(B));
  Multiplexer #(.width(5), .enable("false")) multiplexer_5 (.in0(Rt), .in1({5{1'b1}}), .out(S_S_B), .sel(R_Type_PP));
  Random #(.width(32)) random_1 (.clk(Input), .out(random_1_out));  // open: next, clr
  Multiplexer #(.select(2), .width(32), .enable("false")) multiplexer_6 (
    .in0(Out), .in1(random_1_out), .in2(in_13), .in3(M_I), .out(Inp), .sel(in_10));
  Multiplexer #(.select(2), .width(5), .enable("false")) multiplexer_7 (
    .in0(Rd), .in1(Rt), .in2({5{1'b1}}), .out(DW), .sel(in_6));  // open: in3
  and and_1 (R_W_RF, ~M_D, in_8);  // AND_Gate
  and and_2 (L_H_R_W, M_D, in_8);
  // also tied to VCC on the sheet: {Instruction[0], Instruction[1], Instruction[2], Instruction[3], Instruction[4], Instruction[5], Instruction[6], Instruction[7], Instruction[8], Instruction[9], Instruction[10], Instruction[11], Instruction[12], Instruction[13], Instruction[14], Instruction[15], Instruction[16], Instruction[17], Instruction[18], Instruction[19], Instruction[20], Instruction[21], Instruction[22], Instruction[23], Instruction[24], Instruction[25], Instruction[26], Instruction[27], Instruction[28], Instruction[29], Instruction[30], Instruction[31]}

  // Other names for the same wires on the sheet: Clock = Input; CS = out_17; DATA_RAM[31:0] = out_14;
  //   DIR_RAM[15:0] = out_15; I0[31:0] = in_4; I1[31:0] = in_7; I2[31:0] = in_11; I3[31:0] = in_12; I_Type = out_20;
  //   KBD[31:0] = in_13; L_S = out_23; MASK[3:0] = out_16; PC_enable = in_3; Push_Pop = out_24; R_Time[3:0] = in_5;
  //   R_W__RAM = in_9; R_W__RF = in_8; RAM_R_W = out_18; Reset = in_2; S_DATA__RF[1:0] = in_10; S_DW_RF[1:0] = in_6;
  //   S_Input[1:0] = out_21; S_Special[1:0] = out_22; T_Op[2:0] = out_25; TTY[31:0] = out_19

  // Notes on the sheet:
  //   Data Path
  //   ALU
  //   Program Counter
  //   Instruction Memory
  //   BC
  //   Register File
  //   Instruction Decoder
  //   Output
endmodule

module Instruction_Memory (
  input  [31:0] in_1,
  input  [31:0] in_2,
  input  [31:0] in_3,
  input  [31:0] in_4,
  input  [31:0] Address,
  input  [31:0] in_6,
  output [31:0] out_7,
  output [31:0] out_8,
  output [15:0] Address_2,
  output [3:0] MASK
);

  wire not_1_out, not_2_out, not_3_out, not_4_out;

  and and_1 (MASK[3], Address[2], Address[3]);
  not not_1 (not_1_out, Address[2]);
  not not_2 (not_2_out, Address[3]);
  not not_3 (not_3_out, Address[2]);
  not not_4 (not_4_out, Address[3]);
  and and_2 (MASK[2], not_1_out, Address[3]);
  and and_3 (MASK[1], not_2_out, Address[2]);
  and and_4 (MASK[0], not_3_out, not_4_out);
  Multiplexer #(.select(2), .width(32), .enable("false")) multiplexer_1 (
    .in0(in_1), .in1(in_3), .in2(in_2), .in3(in_4),
    .out({out_7[7:0], out_7[15:8], out_7[23:16], out_7[31:24]}), .sel(Address[3:2]));

  assign Address_2 = Address[19:4];
  assign out_8 = {in_6[7:0], in_6[15:8], in_6[23:16], in_6[31:24]};

  // Other names for the same wires on the sheet: Bank_SEL[1:0] = Address[3:2]; Address_to_RAM[15:0] = Address[19:4];
  //   I0[31:0] = in_1; I1[31:0] = in_3; I2[31:0] = in_2; I3[31:0] = in_4; RD[31:0] = out_7;
  //   WD[31:0] = {in_6[7:0], in_6[15:8], in_6[23:16], in_6[31:24]}
endmodule
